# Fritzing sketch fritzing_patate (saved by Fritzing 0.9.3b)
breadboards: 1

parts:
  R1 = Resistor [tolerance=±5% resistance=10k package=THT]
  L1 = Inductor [inductance=10mH package="400 mil [THT]"]
  R2 = Resistor [tolerance=±5% resistance=3.3k package=THT]
  R3 = Resistor [tolerance=±5% resistance=1M package=THT]
  C1 = Ceramic Capacitor [capacitance=0.1nF package="100 mil [THT, multilayer]"]
  Composant1 = Arduino Uno (Rev3)
  D1 = Rectifier Diode [part_number=1N4148 package="300 mil [THT]"]
  C2 = Ceramic Capacitor [capacitance=10nF package="100 mil [THT, multilayer]"]  # not connected
  LED1 = LED - 5mm [color="Red (633nm)" package="5 mm [THT]"]
  LED2 = LED - 5mm [color="Red (633nm)" package="5 mm [THT]"]

nets:
  N1: R1.Pin_0, L1.pin_1
  N2: R1.Pin_1, Composant1.D9_PWM
  N3: L1.pin_0, D1.anode
  GND: R2.Pin_1, R3.Pin_1, C1.0, Composant1.GND, LED1.cathode, LED2.cathode
  N4: R3.Pin_0, D1.cathode
  N5: Composant1.D4, LED1.anode
  N6: Composant1.D7, LED2.anode

notes:
  Electrode
